# Fritzing sketch LED_steuerung (saved by Fritzing 0.9.9b)
circuit board: 8.45124cm x 6.21543cm
breadboards: 1

parts:
  LED-Streifen_4 = female pin header, 3 pins [form="♀ (female)"]
  LED-Streifen_3 = female pin header, 3 pins [form="♀ (female)"]
  LED-Streifen_2 = female pin header, 3 pins [form="♀ (female)"]
  LED-Streifen_1 = female pin header, 3 pins [form="♀ (female)"]
  5V-Spannungsversorgung = female pin header, 2 pins [form="♀ (female)"]
  U1 = NodeMCU V1.0
  RTC = Adafruit DS3231 [part_number="Adafruit #3013"]
  anschluss_klemme_Mikro = female pin header, 3 pins [form="♀ (female)"]

nets:
  N1: LED-Streifen_4.pin1, LED-Streifen_3.pin1, LED-Streifen_2.pin1, LED-Streifen_1.pin1, 5V-Spannungsversorgung.pin1, U1.Vin, anschluss_klemme_Mikro.pin3
  N2: LED-Streifen_4.pin2, U1.D8
  GND: LED-Streifen_4.pin3, LED-Streifen_3.pin3, LED-Streifen_2.pin3, LED-Streifen_1.pin3, 5V-Spannungsversorgung.pin2, U1.GND, RTC.GND, anschluss_klemme_Mikro.pin2
  N3: LED-Streifen_3.pin2, U1.D7
  N4: LED-Streifen_2.pin2, U1.D6
  N5: LED-Streifen_1.pin2, U1.D5
  N6: U1.D2, RTC.SDA
  N7: U1.D3, RTC.SCL
  3V3: U1.3V3, RTC.Vin
  N8: U1.A0, anschluss_klemme_Mikro.pin1

custom parts:
  NodeMCU V1.0: ESP8266 based NodeMCU
  Adafruit DS3231: The datasheet for the DS3231 explains that this part is an "Extremely Accurate I²C-Integrated RTC/TCXO/Crystal". And, hey, it does exactly what it says on the tin! This Real Time Clock (RTC) is the most precise you can get in a small, low power package. Most RTCs use an external 32kHz timing crystal that is used to keep time with low current draw. And that's all well and good, but those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
